# Fritzing sketch diagram (saved by Fritzing 0.9.4)
breadboards: 1

parts:
  LED1 = LED - 5mm [color="Blue (430nm)" package="5 mm [THT]"]
  LED2 = LED - 5mm [color="Red (633nm)" package="5 mm [THT]"]
  LED3 = LED - 5mm [color="Red (633nm)" package="5 mm [THT]"]
  LED4 = LED - 5mm [color="Yellow (595nm)" package="5 mm [THT]"]
  Part1 = Arduino Nano (Rev3.0)
  R1 = Resistor [tolerance=±5% resistance=220 package=THT]
  R2 = Photocell (LDR) [package=THT]
  R3 = Resistor [tolerance=±5% resistance=220 package=THT]
  R4 = Resistor [tolerance=±5% resistance=220 package=THT]
  R5 = Resistor [tolerance=±5% resistance=220 package=THT]
  R6 = Resistor [tolerance=±5% resistance=220 package=THT]
  J1 = Basic Servo

nets:
  N1: LED1.cathode, R5.Pin_1
  N2: LED1.anode, Part1.D4
  N3: LED2.cathode, R4.Pin_1
  N4: LED2.anode, Part1.D5
  N5: LED3.cathode, R3.Pin_1
  N6: LED3.anode, Part1.D6
  N7: LED4.cathode, R6.Pin_1
  N8: LED4.anode, Part1.D3
  N9: Part1.D2, R1.Pin_0, R3.Pin_0, R4.Pin_0, R5.Pin_0, R6.Pin_0, J1.gnd
  N10: Part1.D7, J1.pulse
  5V: Part1.5V, R2.pin_1, J1.vcc
  N11: Part1.A4, R1.Pin_1, R2.pin_0
